# Fritzing sketch attiny-programmer (saved by Fritzing 0.9.3b)
circuit board: 3.07636cm x 5.16152cm
breadboards: 1

parts:
  attiny85 = attiny85 [package=dip]
  C2 = Electrolytic Capacitor [capacitance=1µF package="100 mil [THT, electrolytic]"]
  S1 = Toggle Switch [package=THT]
  S2 = Toggle Switch [package=THT]
  S3 = Toggle Switch [package=THT]
  S4 = Toggle Switch [package=THT]
  S5 = Toggle Switch [package=THT]
  S7 = Toggle Switch [package=THT]
  S8 = Toggle Switch [package=THT]
  S6 = Toggle Switch [package=THT]
  attiny85_programmer = Arduino Uno (Rev3)
  J1 = female pin header, 8 pins [form="♀ (female)"]

nets:
  N1: attiny85.Pin_1, S5.COM
  N2: attiny85.Pin_2, S6.COM
  N3: attiny85.Pin_3, S7.COM
  N4: attiny85.Pin_4, S8.COM
  N5: attiny85.Pin_5, S4.COM
  N6: attiny85.Pin_6, S3.COM
  N7: attiny85.Pin_7, S2.COM
  N8: attiny85.Pin_8, S1.COM
  N9: C2.-, S1.L2, attiny85_programmer.GND
  N10: C2.+, attiny85_programmer.RESET
  N11: S1.L1, J1.pin8
  N12: S2.L1, J1.pin7
  N13: S3.L1, J1.pin6
  N14: S4.L1, J1.pin5
  N15: S4.L2, attiny85_programmer.D10_PWM/SS
  N16: S5.L1, J1.pin4
  N17: S5.L2, attiny85_programmer.D11_PWM/MOSI
  N18: S7.L1, J1.pin2
  N19: S7.L2, attiny85_programmer.D13/SCK
  N20: S8.L1, J1.pin1
  N21: S8.L2, attiny85_programmer.5V
  N22: S6.L1, J1.pin3
  N23: S6.L2, attiny85_programmer.D12/MISO

notes:
  +
  2 A1
  1
  0
  rst
  gnd
  3 A3
  4 A2
  -
  3
  4
  2
